# Fritzing sketch circuit (saved by Fritzing 0.9.10b)
breadboards: 1

parts:
  Componente1 = Arduino Nano (Rev3.0)
  Part3 = RFID-RC522-v3
  LED1 = smd LED [color="Red (633nm)" package="1206 [SMD]"]
  LED2 = smd LED [color="Green (555nm)" package="1206 [SMD]"]
  M1 = 1 chan 5v relay module

nets:
  GND: Componente1.GND, Componente1.D7, Part3.GND, LED1.cathode, LED2.cathode, M1.pin_2, M1.pin_3
  N1: Componente1.D9, Part3.RST
  N2: Componente1.D10, Part3.SDA
  N3: Componente1.D11/MOSI, Part3.MOSI
  N4: Componente1.D12/MISO, Part3.MISO
  N5: Componente1.VIN, M1.pin_1
  3V3: Componente1.3V3, Part3.3.3V
  N6: Componente1.D13/SCK, Part3.SCK

custom parts:
  RFID-RC522-v3: A simple China made RFID-RC522 Reader (6x4 cm); do check the pin labels, as this is a MFRC522 based clone.
  1 chan 5v relay module: 1 Channel 5V Relay Module Board Shield with Optocoupler Support High and Low Level Trigger for Arduino.
